# Fritzing sketch player (saved by Fritzing 0.9.9b)
stripboards: 1

parts:
  MCP3008 = MCP3008 [package=dil16]
  R1 = Resistor [tolerance=±5% power=0.25 resistance=220 package=THT]
  Part1 = Adafruit Stereo 3W Speaker Bonnet [part_number="Adafruit #"]
  J2 = female pin header, 7 pins [form="♀ (female)"]
  J3 = female pin header, 7 pins [form="♀ (female)"]
  J4 = female pin header, 7 pins [form="♀ (female)"]
  J6 = female pin header, 8 pins [form="♀ (female)"]
  J5 = female pin header, 8 pins [form="♀ (female)"]
  J7 = female pin header, 6 pins [form="♀ (female)"]
  J8 = female pin header, 1 pin [form="♀ (female)"]
  J9 = female pin header, 1 pin [form="♀ (female)"]
  J10 = female pin header, 4 pins [form="♀ (female)"]
  S1 = Round Pushbutton
  S2 = Round Pushbutton
  S3 = Round Pushbutton
  S4 = Round Pushbutton
  S5 = Round Pushbutton
  S6 = Round Pushbutton
  S7 = Round Pushbutton
  U1 = POT_SWITCH [package=pot_pth]
  LED1 = smd LED [color="Green (560nm)" package="1206 [SMD]"]
  SP1 = SPEAKER [package=pcb_mount_speaker]
  SP2 = SPEAKER [package=pcb_mount_speaker]

nets:
  N1: MCP3008.CH0, J6.pin1, J7.pin6, U1.G$2_1
  N2: MCP3008.CH1, J6.pin2
  N3: MCP3008.CH2, J6.pin3
  N4: MCP3008.CH3, J6.pin4
  N5: MCP3008.CH4, J6.pin5
  N6: MCP3008.CH5, J6.pin6
  N7: MCP3008.CH6, J6.pin7
  N8: MCP3008.CH7, J6.pin8
  N9: MCP3008.DGND, MCP3008.CS/SHDN, R1.Pin_0, Part1.SPI_MOSI, Part1.GND, J5.pin7, J5.pin8, J7.pin4, J8.pin1, J10.pin4, U1.G$1_E, LED1.cathode
  N10: MCP3008.Din, Part1.SPI_MISO, J5.pin6, J10.pin3
  N11: MCP3008.Dout, Part1.SPI_SCLK, J5.pin5, J10.pin2
  N12: MCP3008.CLK, Part1.SPI_CE0, J5.pin4, J10.pin1
  N13: MCP3008.AGND, J5.pin3
  N14: MCP3008.VREF, J5.pin2
  VDD: MCP3008.VDD, Part1.3.3V, J5.pin1, J7.pin5, J9.pin1, U1.G$1_A
  N15: R1.Pin_1, J3.pin1, S4.leg1
  N16: Part1.SCL, J7.pin1, J7.pin2, U1.G$1_S
  N17: Part1.TXD, LED1.anode
  N18: Part1.GPIO24, J2.pin7, J4.pin7, S7.leg0
  N19: Part1.GPIO5, J2.pin6, J4.pin6, S6.leg0
  N20: Part1.GPIO6, J2.pin5, J4.pin5, S5.leg0
  N21: Part1.GPIO12, J2.pin4, J4.pin4, S1.leg0
  N22: Part1.GPIO13, J2.pin3, J4.pin3, S3.leg0
  N23: Part1.GPIO16, J2.pin2, J4.pin2, S2.leg0
  N24: Part1.GPIO20, J2.pin1, J4.pin1, S4.leg0
  N25: Part1.RIGHT-, SP2.+
  N26: Part1.RIGHT+, SP2.-
  N27: Part1.LEFT+, SP1.-
  N28: Part1.LEFT-, SP1.+
  N29: J3.pin2, S2.leg1
  N30: J3.pin3, S3.leg1
  N31: J3.pin4, S1.leg1
  N32: J3.pin5, S5.leg1
  N33: J3.pin6, S6.leg1
  N34: J3.pin7, S7.leg1
  N35: J7.pin3, U1.G$2_2

notes:
  Florence Player
  Shutdown switch
  Station1
  Station2
  Station3
  Station4
  Play
  Pause
  Skip

custom parts:
  Adafruit Stereo 3W Speaker Bonnet: Hey Mr. DJ! Turn up that Raspberry Pi mix to the max with this cute 3W Stereo Amplifier Bonnet for Raspberry Pi. (It's not big enough to be an official HAT, so we called it a bonnet, you see?) It's the exact same size as a Raspberry Pi Zero but works with any and all Raspberry Pi computers with a 2x20 connector - A+, B+, Zero, Pi 2, Pi 3, etc. This Bonnet uses I2S a digital sound standard, so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
