# Fritzing sketch player_stripboard_no_components (saved by Fritzing 0.9.9b)
stripboards: 1

parts:
  J20 = female pin header, 6 pins [form="♀ (female)"]
  J21 = female pin header, 8 pins [form="♀ (female)"]
  J22 = female pin header, 8 pins [form="♀ (female)"]
  J23 = female pin header, 7 pins [form="♀ (female)"]
  J24 = female pin header, 7 pins [form="♀ (female)"]  # not connected
  J25 = female pin header, 7 pins [form="♀ (female)"]
  J26 = female pin header, 1 pin [form="♀ (female)"]
  J27 = female pin header, 1 pin [form="♀ (female)"]
  J28 = female pin header, 4 pins [form="♀ (female)"]

nets:
  N1: J20.pin1, J20.pin2
  N2: J20.pin4, J21.pin7, J21.pin8, J26.pin1, J28.pin4
  N3: J20.pin5, J21.pin1, J27.pin1
  N4: J20.pin6, J22.pin1
  N5: J21.pin4, J28.pin1
  N6: J21.pin5, J28.pin2
  N7: J21.pin6, J28.pin3
  N8: J23.pin1, J25.pin1
  N9: J23.pin2, J25.pin2
  N10: J23.pin3, J25.pin3
  N11: J23.pin4, J25.pin4
  N12: J23.pin5, J25.pin5
  N13: J23.pin6, J25.pin6
  N14: J23.pin7, J25.pin7
